// Logisim project lab02.circ as structural Verilog
module half_sum (
  input  A,
  input  B,
  output S,
  output \С 
);

  xor xor_1 (S, A, B);
  and and_1 (\С , A, B);
endmodule

module sum (
  input  CI,
  input  A,
  input  B,
  output S,
  output CO
);

  wire half_sum_1_s, \half_sum_1_с , \half_sum_2_с ;

  half_sum half_sum_1 (.A(A), .S(half_sum_1_s), .B(B), .\С (\half_sum_1_с ));
  half_sum half_sum_2 (.A(CI), .S(S), .B(half_sum_1_s), .\С (\half_sum_2_с ));
  or or_1 (CO, \half_sum_2_с , \half_sum_1_с );
endmodule

module _8bit_sum (
  input  [7:0] A,
  input  CI,
  input  [7:0] B,
  output CO,
  output [7:0] SUM
);

  wire sum_2_co, sum_3_co, sum_4_co, sum_5_co, sum_6_co, sum_7_co, sum_8_co;

  // Probe on A
  // Probe on B
  // Probe on SUM
  sum sum_1 (.CI(sum_2_co), .A(A[7]), .B(B[7]), .S(SUM[7]), .CO(CO));
  sum sum_2 (.CI(sum_3_co), .A(A[6]), .B(B[6]), .S(SUM[6]), .CO(sum_2_co));
  sum sum_3 (.CI(sum_4_co), .A(A[5]), .B(B[5]), .S(SUM[5]), .CO(sum_3_co));
  sum sum_4 (.CI(sum_5_co), .A(A[4]), .B(B[4]), .S(SUM[4]), .CO(sum_4_co));
  sum sum_5 (.CI(sum_6_co), .A(A[3]), .B(B[3]), .S(SUM[3]), .CO(sum_5_co));
  sum sum_6 (.CI(sum_7_co), .A(A[2]), .B(B[2]), .S(SUM[2]), .CO(sum_6_co));
  sum sum_7 (.CI(sum_8_co), .A(A[1]), .B(B[1]), .S(SUM[1]), .CO(sum_7_co));
  sum sum_8 (.CI(CI), .A(A[0]), .B(B[0]), .S(SUM[0]), .CO(sum_8_co));
endmodule

module inventor (
  input  A,
  input  CI,
  output NOT_A
);

  xor xor_1 (NOT_A, A, CI);
endmodule

module _8bit_inventor (
  input  CI,
  input  [7:0] A,
  output [7:0] NOT_A
);

  inventor inventor_1 (.A(A[0]), .NOT_A(NOT_A[0]), .CI(CI));
  inventor inventor_2 (.A(A[2]), .NOT_A(NOT_A[2]), .CI(CI));
  inventor inventor_3 (.A(A[1]), .NOT_A(NOT_A[1]), .CI(CI));
  inventor inventor_4 (.A(A[3]), .NOT_A(NOT_A[3]), .CI(CI));
  inventor inventor_5 (.A(A[4]), .NOT_A(NOT_A[4]), .CI(CI));
  inventor inventor_6 (.A(A[6]), .NOT_A(NOT_A[6]), .CI(CI));
  inventor inventor_7 (.A(A[5]), .NOT_A(NOT_A[5]), .CI(CI));
  inventor inventor_8 (.A(A[7]), .NOT_A(NOT_A[7]), .CI(CI));
endmodule

module subtraction (
  input  [7:0] A,
  input  [7:0] B,
  input  CS,
  output CO,
  output [7:0] ANSW
);

  wire n8bit_sum_1_co;
  wire [7:0] n8bit_inventor_1_not_a;

  // Probe on A
  // Probe on B
  // Probe on n8bit_inventor_1_not_a
  _8bit_inventor u_8bit_inventor_1 (.A(B), .NOT_A(n8bit_inventor_1_not_a), .CI(CS));
  _8bit_sum u_8bit_sum_1 (.A(A), .B(n8bit_inventor_1_not_a), .SUM(ANSW), .CI(CS), .CO(n8bit_sum_1_co));
  // Probe on ANSW
  inventor inventor_1 (.A(n8bit_sum_1_co), .NOT_A(CO), .CI(CS));
  // Probe on ANSW
endmodule

module multiplay (
  input  [3:0] A,
  input  [3:0] B,
  output [7:0] ANSW
);

  wire A1B2_out, A1B3_out, A1B4_out, A2B1_out, A2B2_out, A2B3_out, A2B4_out, A3B1_out, A3B2_out, A3B3_out,
       A3B4_out, A4B1_out, A4B2_out, A4B3_out, A4B4_out, sum_1_co, sum_2_co, sum_2_s, sum_3_co, sum_4_co,
       sum_4_s, sum_5_co, sum_5_s, sum_6_co, sum_6_s, sum_7_co, sum_7_s, sum_8_co, sum_9_co, sum_9_s,
       sum_10_co, sum_12_co;

  // Probe on A
  // Probe on B
  and A1B1 (ANSW[0], A[0], B[0]);
  // Probe on ANSW
  and A3B1 (A3B1_out, A[2], B[0]);
  and A2B1 (A2B1_out, A[1], B[0]);
  and A1B2 (A1B2_out, A[0], B[1]);
  sum sum_1 (.CI(1'b0), .A(A1B2_out), .B(A2B1_out), .S(ANSW[1]), .CO(sum_1_co));
  and A3B2 (A3B2_out, A[2], B[1]);
  and A2B2 (A2B2_out, A[1], B[1]);
  and A4B1 (A4B1_out, B[1], A[3], B[0], A[2]);
  sum sum_2 (.CI(sum_1_co), .A(A2B2_out), .B(A3B1_out), .S(sum_2_s), .CO(sum_2_co));
  sum sum_3 (.CI(1'b0), .A(A1B3_out), .B(sum_2_s), .S(ANSW[2]), .CO(sum_3_co));
  and A4B2 (A4B2_out, A[3], B[1]);
  sum sum_4 (.CI(sum_2_co), .A(A3B2_out), .B(A4B1_out), .S(sum_4_s), .CO(sum_4_co));
  sum sum_5 (.CI(sum_3_co), .A(A2B3_out), .B(sum_4_s), .S(sum_5_s), .CO(sum_5_co));
  and A1B3 (A1B3_out, A[0], B[2]);
  sum sum_6 (.CI(sum_4_co), .A(1'b0), .B(A4B2_out), .S(sum_6_s), .CO(sum_6_co));
  sum sum_7 (.CI(sum_5_co), .A(A3B3_out), .B(sum_6_s), .S(sum_7_s), .CO(sum_7_co));
  sum sum_8 (.CI(1'b0), .A(A1B4_out), .B(sum_5_s), .S(ANSW[3]), .CO(sum_8_co));
  and A3B3 (A3B3_out, A[2], B[2]);
  and A2B3 (A2B3_out, A[1], B[2]);
  and A4B3 (A4B3_out, A[3], B[2]);
  sum sum_9 (.CI(sum_7_co), .A(A4B3_out), .B(sum_6_co), .S(sum_9_s), .CO(sum_9_co));
  sum sum_10 (.CI(sum_8_co), .A(A2B4_out), .B(sum_7_s), .S(ANSW[4]), .CO(sum_10_co));
  and A2B4 (A2B4_out, A[1], B[3]);
  and A1B4 (A1B4_out, A[0], B[3]);
  sum sum_11 (.CI(sum_12_co), .A(A4B4_out), .B(sum_9_co), .S(ANSW[6]), .CO(ANSW[7]));
  sum sum_12 (.CI(sum_10_co), .A(A3B4_out), .B(sum_9_s), .S(ANSW[5]), .CO(sum_12_co));
  and A4B4 (A4B4_out, A[3], B[3]);
  and A3B4 (A3B4_out, A[2], B[3]);
endmodule

module right_cycl_shift (
  input  in_1,
  input  [3:0] in_2,
  output [3:0] out_3
);

  Transistor #(.\type ("n")) transistor_1 (.in(in_2[0]), .out(out_3[3]), .gate(in_1));
  Transistor #(.\type ("n")) transistor_2 (.in(in_2[1]), .out(out_3[0]), .gate(in_1));
  Transistor #(.\type ("n")) transistor_3 (.in(in_2[2]), .out(out_3[1]), .gate(in_1));
  Transistor #(.\type ("n")) transistor_4 (.in(in_2[3]), .out(out_3[2]), .gate(in_1));
  Transistor transistor_5 (.in(in_2[0]), .out(out_3[0]), .gate(in_1));
  Transistor transistor_6 (.in(in_2[1]), .out(out_3[1]), .gate(in_1));
  Transistor transistor_7 (.in(in_2[2]), .out(out_3[2]), .gate(in_1));
  Transistor transistor_8 (.in(in_2[3]), .out(out_3[3]), .gate(in_1));
endmodule

module left_cycl_shift (
  input  in_1,
  input  [3:0] in_2,
  output [3:0] out_3
);

  Transistor #(.\type ("n")) transistor_1 (.in(in_2[0]), .out(out_3[1]), .gate(in_1));
  Transistor #(.\type ("n")) transistor_2 (.in(in_2[1]), .out(out_3[2]), .gate(in_1));
  Transistor #(.\type ("n")) transistor_3 (.in(in_2[2]), .out(out_3[3]), .gate(in_1));
  Transistor #(.\type ("n")) transistor_4 (.in(in_2[3]), .out(out_3[0]), .gate(in_1));
  Transistor transistor_5 (.in(in_2[0]), .out(out_3[0]), .gate(in_1));
  Transistor transistor_6 (.in(in_2[1]), .out(out_3[1]), .gate(in_1));
  Transistor transistor_7 (.in(in_2[2]), .out(out_3[2]), .gate(in_1));
  Transistor transistor_8 (.in(in_2[3]), .out(out_3[3]), .gate(in_1));
endmodule

module right_arfm_shift (
  input  in_1,
  input  [3:0] in_2,
  output [3:0] out_3
);

  Transistor #(.\type ("n")) transistor_1 (.in(in_2[1]), .out(out_3[0]), .gate(in_1));
  Transistor #(.\type ("n")) transistor_2 (.in(in_2[2]), .out(out_3[1]), .gate(in_1));
  Transistor #(.\type ("n")) transistor_3 (.in(in_2[3]), .out(out_3[2]), .gate(in_1));
  Transistor transistor_4 (.in(in_2[1]), .out(out_3[1]), .gate(in_1));
  Transistor transistor_5 (.in(in_2[2]), .out(out_3[2]), .gate(in_1));
  Transistor transistor_6 (.in(in_2[0]), .out(out_3[0]), .gate(in_1));

  assign out_3[3] = in_2[3];
endmodule

module left_arifm_shift (
  input  in_1,
  input  [3:0] in_2,
  output [3:0] out_3
);

  // Probe on in_2
  Transistor #(.\type ("n")) transistor_1 (.in(1'b0), .out(out_3[0]), .gate(in_1));
  Transistor #(.\type ("n")) transistor_2 (.in(in_2[1]), .out(out_3[2]), .gate(in_1));
  Transistor #(.\type ("n")) transistor_3 (.in(in_2[0]), .out(out_3[1]), .gate(in_1));
  Transistor transistor_4 (.in(in_2[1]), .out(out_3[1]), .gate(in_1));
  Transistor transistor_5 (.in(in_2[2]), .out(out_3[2]), .gate(in_1));
  Transistor transistor_6 (.in(in_2[0]), .out(out_3[0]), .gate(in_1));
  // Probe on {in_2[3], out_3[2:0]}

  assign out_3[3] = in_2[3];
endmodule

module right_log_shift (
  input  in_1,
  input  [3:0] in_2,
  output [3:0] out_3
);

  Transistor #(.\type ("n")) transistor_1 (.in(1'b0), .out(out_3[3]), .gate(in_1));
  Transistor #(.\type ("n")) transistor_2 (.in(in_2[3]), .out(out_3[2]), .gate(in_1));
  Transistor #(.\type ("n")) transistor_3 (.in(in_2[2]), .out(out_3[1]), .gate(in_1));
  Transistor #(.\type ("n")) transistor_4 (.in(in_2[1]), .out(out_3[0]), .gate(in_1));
  Transistor transistor_5 (.in(in_2[0]), .out(out_3[0]), .gate(in_1));
  Transistor transistor_6 (.in(in_2[1]), .out(out_3[1]), .gate(in_1));
  Transistor transistor_7 (.in(in_2[2]), .out(out_3[2]), .gate(in_1));
  Transistor transistor_8 (.in(in_2[3]), .out(out_3[3]), .gate(in_1));
endmodule

module left_log_shift (
  input  in_1,
  input  [3:0] in_2,
  output [3:0] out_3
);

  // Probe on in_2
  Transistor #(.\type ("n")) transistor_1 (.in(1'b0), .out(out_3[0]), .gate(in_1));
  Transistor #(.\type ("n")) transistor_2 (.in(in_2[1]), .out(out_3[2]), .gate(in_1));
  Transistor #(.\type ("n")) transistor_3 (.in(in_2[0]), .out(out_3[1]), .gate(in_1));
  Transistor #(.\type ("n")) transistor_4 (.in(in_2[2]), .out(out_3[3]), .gate(in_1));
  Transistor transistor_5 (.in(in_2[0]), .out(out_3[0]), .gate(in_1));
  Transistor transistor_6 (.in(in_2[1]), .out(out_3[1]), .gate(in_1));
  Transistor transistor_7 (.in(in_2[2]), .out(out_3[2]), .gate(in_1));
  Transistor transistor_8 (.in(in_2[3]), .out(out_3[3]), .gate(in_1));
  // Probe on out_3
endmodule

module _2bit_sum (
  input  CI,
  input  [1:0] A,
  input  [1:0] B,
  output [1:0] SUM,
  output CO
);

  wire sum_1_co;

  sum sum_1 (.CI(CI), .A(A[0]), .B(B[0]), .S(SUM[0]), .CO(sum_1_co));
  sum sum_2 (.CI(sum_1_co), .A(A[1]), .B(B[1]), .S(SUM[1]), .CO(CO));
endmodule

module _2bit_sum_carno (
  input  [1:0] in_1,
  input  [1:0] in_2,
  output [2:0] out_3
);

  wire and_1_out, and_2_out, and_3_out, and_4_out, and_5_out, and_6_out, and_7_out, and_8_out, and_9_out,
       and_10_out, and_11_out, not_1_out, not_2_out, not_3_out, not_4_out, not_5_out, not_6_out, not_7_out,
       not_8_out, not_9_out, not_10_out, not_11_out, not_12_out;

  // Probe on in_1
  // Probe on in_2
  and and_1 (and_1_out, in_1[1], in_2[1]);
  and and_2 (and_2_out, in_1[1], in_1[0], in_2[0]);
  and and_3 (and_3_out, in_1[0], in_2[1], in_2[0]);
  not not_1 (not_1_out, in_1[0]);
  and and_4 (and_4_out, in_1[1], not_1_out, not_2_out);
  not not_2 (not_2_out, in_2[1]);
  not not_3 (not_3_out, in_2[1]);
  and and_5 (and_5_out, in_1[1], not_3_out, not_4_out);
  not not_4 (not_4_out, in_2[0]);
  not not_5 (not_5_out, in_1[1]);
  not not_6 (not_6_out, in_1[0]);
  and and_6 (and_6_out, not_5_out, not_6_out, in_2[1]);
  not not_7 (not_7_out, in_1[1]);
  not not_8 (not_8_out, in_2[0]);
  and and_7 (and_7_out, not_7_out, not_8_out, in_2[1]);
  not not_9 (not_9_out, in_1[1]);
  and and_8 (and_8_out, not_9_out, in_1[0], not_10_out, in_2[0]);
  not not_10 (not_10_out, in_2[1]);
  and and_9 (and_9_out, in_1[1], in_1[0], in_2[1], in_2[0]);
  and and_10 (and_10_out, in_1[0], not_11_out);
  not not_11 (not_11_out, in_2[0]);
  not not_12 (not_12_out, in_1[0]);
  and and_11 (and_11_out, not_12_out, in_2[0]);
  or or_1 (out_3[2], and_1_out, and_2_out, and_3_out);
  or or_2 (out_3[1], and_4_out, and_5_out, and_6_out, and_7_out, and_8_out, and_9_out);
  or or_3 (out_3[0], and_10_out, and_11_out);
  // Probe on out_3
endmodule
